# Fritzing sketch Qwiic_Tile_3231M_RTC_v1 (saved by Fritzing 0.9.3b)
circuit board: 1.84cm x 2.54cm
breadboards: 1

parts:
  Qwiic = Qwiic JST [package=1x04-1mm-ra]
  Qwiic_2 = Qwiic JST [package=1x04-1mm-ra]
  DS3231M = SO08 [chip_label=DS3231M package=SO]
  BAT1 = Battery Holders [package=battcon_20mm_4legs]
  DS3231M1 = SO08 [chip_label=DS3231M package=SO]  # not connected
  4_7K = Resistor [tolerance=±5% resistance=4.7k package="0805 [SMD]"]
  4_7K_2 = Resistor [tolerance=±5% resistance=4.7k package="0805 [SMD]"]
  0_1uF = Ceramic Capacitor [capacitance=0.1µF package="0805 [SMD, multilayer]"]
  J1 = female pin header, 4 pins [form="♀ (female)"]
  0_1uF_2 = Ceramic Capacitor [capacitance=0.1µF package="0805 [SMD, multilayer]"]

nets:
  N1: Qwiic.1, Qwiic_2.1, DS3231M.GND, BAT1.-, 0_1uF.1, J1.pin4, 0_1uF_2.1
  N2: Qwiic.2, Qwiic_2.2, DS3231M.3v3, 4_7K.Pin_1, 4_7K_2.Pin_1, J1.pin3, 0_1uF_2.0
  N3: Qwiic.3, Qwiic_2.3, DS3231M.SDA, 4_7K.Pin_0, J1.pin2
  N4: Qwiic.4, Qwiic_2.4, DS3231M.SCL, 4_7K_2.Pin_0, J1.pin1
  N5: DS3231M.VBatt, BAT1.+, 0_1uF.0

custom parts:
  Qwiic JST: Header 4 Standard 4-pin 0.1 header. Use with straight break away headers (SKU : PRT-00116), right angle break away headers (PRT-00553), swiss pins (PRT-00743), machine pins (PRT-00117), and female headers (PRT-00115). Molex polarized connector foot print use with SKU : PRT-08231 with associated crimp pins and housings. 1MM SMD Version SKU: PRT-10208
