# Fritzing sketch RFMX9HCW_Stamp_v1 (saved by Fritzing 0.9.3b)
circuit board: 2cm x 2cm
breadboards: 1

parts:
  Part1 = RFM69W  # not connected
  Part2 = Adafruit ItsyBitsy M4 [part_number="Adafruit #3800"]  # not connected
  J1 = female pin header, 8 pins [form="♀ (female)"]
  J2 = female pin header, 8 pins [form="♀ (female)"]
  Pad1 = Pad [width=2 height=1 connect=center]  # not connected
  Pad2 = Pad [width=2 height=1 connect=center]  # not connected
  Pad3 = Pad [width=2 height=1 connect=center]  # not connected
  Pad4 = Pad [width=2 height=1 connect=center]  # not connected
  Pad5 = Pad [width=2 height=1 connect=center]  # not connected
  Pad6 = Pad [width=2 height=1 connect=center]  # not connected
  Pad7 = Pad [width=2 height=1 connect=center]  # not connected
  Pad8 = Pad [width=2 height=1 connect=center]  # not connected
  Pad9 = Pad [width=2 height=1 connect=center]  # not connected
  Pad10 = Pad [width=2 height=1 connect=center]  # not connected
  Pad11 = Pad [width=2 height=1 connect=center]  # not connected
  Pad12 = Pad [width=2 height=1 connect=center]  # not connected
  Pad13 = Pad [width=2 height=1 connect=center]  # not connected
  Pad14 = Pad [width=2 height=1 connect=center]  # not connected
  Pad15 = Pad [width=2 height=1 connect=center]  # not connected
  Pad16 = Pad [width=2 height=1 connect=center]  # not connected
  J4 = shrouded pin header, 10 pins [form="♂ (shrouded male)"]  # not connected
  Pad17 = Pad [width=1.8 height=3 connect=center]
  Pad18 = Pad [width=1.8 height=3 connect=center]
  Pad19 = Pad [width=1.8 height=3 connect=center]
  Pad20 = Pad [width=1.8 height=3 connect=center]
  Pad21 = Pad [width=1.8 height=3 connect=center]
  Pad26 = Pad [width=1.8 height=3 connect=center]  # not connected
  Pad22 = Pad [width=1.8 height=3 connect=center]  # not connected
  Pad25 = Pad [width=1.8 height=3 connect=center]
  Pad23 = Pad [width=1.8 height=3 connect=center]
  Pad24 = Pad [width=1.8 height=3 connect=center]
  RFM1 = RFM69HCW ISM Transciever  # not connected
  C1 = Tantalum Capacitor [capacitance=10µF package="B 3528 [SMD, tantalum]"]  # not connected
  10uF = Ceramic Capacitor [capacitance=1µF package="1206 [SMD, multilayer]"]
  u_FL = U.FL [package=u.fl]

nets:
  N1: J1.pin1, u_FL.SIGNAL
  N2: J1.pin2, Pad24.pad
  N3: J1.pin5, Pad17.pad, 10uF.0
  N4: J1.pin6, Pad23.pad
  N5: J2.pin1, J2.pin8, 10uF.1, u_FL.GND
  N6: J2.pin3, Pad25.pad
  N7: J2.pin4, Pad18.pad
  N8: J2.pin5, Pad19.pad
  N9: J2.pin6, Pad20.pad
  N10: J2.pin7, Pad21.pad

notes:
  A HighJinx Joint
  RFMX9HCW Stamp v1
  RST
  INT
  GND
  3v3
  CS
  SCK
  MOSI
  MISO

custom parts:
  Adafruit ItsyBitsy M4: What's smaller than a Feather but larger than a Trinket? It's an Adafruit ItsyBitsy M4 Express featuring the Microchip ATSAMD51! Small, powerful, with a ultra fast ATSAMD51 Cortex M4 processor running at 120 MHz - this microcontroller board is perfect when you want something very compact, with a ton of horsepower and a bunch of pins. This Itsy is like a bullet train, with it's 120MHz Cortex M4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
  RFM69HCW ISM Transciever: RF Transceiver by Hope RF. Well supported Arduino libraries are available. This ISM band transceiver is available in several frequencies e.g. 433MHz and 915MHz and it is also available in various feature versions.
  U.FL: SMD antenna connector- WRL-09144
