# Fritzing sketch Scoots_EDP_Mainboard_v1 (saved by Fritzing 0.9.3b)
circuit board: 4.3cm x 3.00435cm
breadboards: 1

parts:
  Part2 = Adafruit Feather M0 Express [part_number="Adafruit #3403"]  # not connected
  J3 = female pin header, 16 pins [form="♀ (female)"]  # not connected
  J6 = female pin header, 2 pins [form="♀ (female)"]  # not connected
  J7 = female pin header, 12 pins [form="♀ (female)"]
  J8 = female pin header, 16 pins [form="♀ (female)"]
  ESC = Qwiic JST [package=1x04-1mm-ra]
  J4 = female pin header, 12 pins [form="♀ (female)"]
  J5 = female pin header, 16 pins [form="♀ (female)"]
  Qwiic = Qwiic JST [package=1x04-1mm-ra]
  HV = female pin header, 6 pins [form="♀ (female)"]
  LV = female pin header, 6 pins [form="♀ (female)"]
  Lights = longpad pin header, 4 pins [form="long pad"]
  HV_Cap = Electrolytic Capacitor [capacitance=1µF package="100 mil [THT, electrolytic]"]
  Throttle = longpad pin header, 4 pins [form="long pad"]
  Batt_+ = Pad [width=2.25 height=2.25 connect=center]
  CR12x2_Battery = Pad [width=2.25 height=2.25 connect=center]
  Batt_- = Pad [width=2.25 height=2.25 connect=center]
  10㎌1 = Ceramic Capacitor [capacitance=10µF package="1206 [SMD, multilayer]"]
  4k7 = Ceramic Capacitor [capacitance=1µF package="1206 [SMD, multilayer]"]
  4k7_2 = Ceramic Capacitor [capacitance=1µF package="1206 [SMD, multilayer]"]
  1uF = Ceramic Capacitor [capacitance=1µF package="1206 [SMD, multilayer]"]
  DS3231M = SO08 [chip_label=DS3231M package=SO]

nets:
  N1: J7.pin1, J4.pin1, Qwiic.3, 4k7_2.1, DS3231M.7
  N2: J7.pin2, J4.pin2, Qwiic.4, 4k7.1, DS3231M.8
  N3: J7.pin3, J4.pin3
  N4: J7.pin4, J4.pin4
  N5: J7.pin5, J4.pin5
  N6: J7.pin6, J4.pin6
  N7: J7.pin7, J4.pin7, LV.pin1
  N8: J7.pin8, J4.pin8, LV.pin2
  N9: J7.pin9, J4.pin9
  N10: J7.pin10, J4.pin10
  N11: J7.pin11, J4.pin11
  N12: J7.pin12, ESC.2, J4.pin12, HV.pin4, Lights.pin2, HV_Cap.+
  N13: J8.pin1, J5.pin1
  N14: J8.pin2, J5.pin2, LV.pin5
  N15: J8.pin3, J5.pin3, LV.pin6
  N16: J8.pin4, J5.pin4
  N17: J8.pin5, J5.pin5
  N18: J8.pin6, J5.pin6
  N19: J8.pin7, J5.pin7
  N20: J8.pin8, J5.pin8
  N21: J8.pin9, J5.pin9
  N22: J8.pin10, J5.pin10
  N23: J8.pin11, J5.pin11
  N24: J8.pin12, J5.pin12, Throttle.pin2
  N25: J8.pin13, ESC.1, J5.pin13, Qwiic.1, HV.pin3, LV.pin3, Lights.pin1, HV_Cap.-, Throttle.pin1, Throttle.pin4, CR12x2_Battery.pad, 10㎌1.1, 1uF.0, DS3231M.5
  N26: J8.pin14, J5.pin14
  N27: J8.pin15, J5.pin15, Qwiic.2, LV.pin4, Throttle.pin3, 10㎌1.0, 4k7.0, 4k7_2.0, 1uF.1, DS3231M.2
  N28: J8.pin16, J5.pin16
  N29: ESC.3, HV.pin5
  N30: ESC.4, HV.pin6
  N31: HV.pin1, Lights.pin4
  N32: HV.pin2, Lights.pin3
  N33: Batt_+.pad, Batt_-.pad, DS3231M.6

notes:
  GND
  3V3
  SIG
  G
  5v
  NPf
  NPr
  Lf
  3v3
  Tx
  Rx
  Frt
  Bck
  🙈
  A HighJinx Joint
  Scoots Shield v1
  SAMD51 Feather
  2.13" eInk Featherwing
  DS3231M RTC
  CR12x2 Battery

custom parts:
  Adafruit Feather M0 Express: We love all our Feathers equally, but this Feather is very special. It's our first Feather that is specifically designed for use with CircuitPython! CircuitPython is our beginner-oriented flavor of MicroPython - and as the name hints at, its a small but full-featured version of the popular Python programming language specifically for use with circuitry and electronics. That doesn't mean you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
  Qwiic JST: Header 4 Standard 4-pin 0.1 header. Use with straight break away headers (SKU : PRT-00116), right angle break away headers (PRT-00553), swiss pins (PRT-00743), machine pins (PRT-00117), and female headers (PRT-00115). Molex polarized connector foot print use with SKU : PRT-08231 with associated crimp pins and housings. 1MM SMD Version SKU: PRT-10208
