# Fritzing sketch Scoots_M4AirliftLite_2_3.5TFT_Feather_Shield_v1 (saved by Fritzing 0.9.3b)
circuit board: 6cm x 5.2cm
breadboards: 1

parts:
  Part1 = Adafruit Metro M4 AirLift Lite [part_number="Adafruit #4000"]  # not connected
  J15 = female pin header, 6 pins [form="♀ (female)"]
  J16 = female pin header, 8 pins [form="♀ (female)"]
  J17 = female pin header, 8 pins [form="♀ (female)"]
  J18 = female pin header, 10 pins [form="♀ (female)"]
  J19 = female pin header, 12 pins [form="♀ (female)"]
  J20 = female pin header, 16 pins [form="♀ (female)"]
  J21 = double row female pin header, 6 pins [form="♀ (female)"]
  Qwiic = Qwiic JST [package=1x04-1mm-ra]
  Qwiic_2 = Qwiic JST [package=1x04-1mm-ra]  # not connected
  LV1 = female pin header, 6 pins [form="♀ (female)"]  # not connected
  HV1 = female pin header, 6 pins [form="♀ (female)"]  # not connected
  DS3231M = SO08 [chip_label=DS3231M package=SO]
  1uF = Ceramic Capacitor [capacitance=1µF package="1206 [SMD, multilayer]"]
  4k7 = Ceramic Capacitor [capacitance=1µF package="1206 [SMD, multilayer]"]
  4k7_2 = Ceramic Capacitor [capacitance=1µF package="1206 [SMD, multilayer]"]
  DS3231M_2 = SO08 [chip_label=DS3231M package=SO]
  4k7_3 = Ceramic Capacitor [capacitance=1µF package="1206 [SMD, multilayer]"]
  4k7_4 = Ceramic Capacitor [capacitance=1µF package="1206 [SMD, multilayer]"]
  1uF_2 = Ceramic Capacitor [capacitance=1µF package="1206 [SMD, multilayer]"]
  0_1uF = Ceramic Capacitor [capacitance=0.1µF package="1206 [SMD, multilayer]"]
  BAT3 = Battery Holders [package=battcon_20mm_4legs]
  ESC = Qwiic JST [package=1x04-1mm-ra]
  J22 = female pin header, 3 pins [form="♀ (female)"]
  Thr-Sig = Pad [width=2.7657777777777888 height=1.6368888888888919 connect=center]
  Thr-Pos = Pad [width=2.7657777777777888 height=1.6368888888888919 connect=center]
  Thr-Gnd = Pad [width=2.7657777777777888 height=1.6368888888888919 connect=center]
  Pad2 = Pad [width=0.84666666666665868 height=0.90311111111111386 connect=center]
  Pad1 = Pad [width=0.84666666666665868 height=0.90311111111111386 connect=center]
  HV3 = female pin header, 4 pins [form="♀ (female)"]
  LV = female pin header, 4 pins [form="♀ (female)"]
  J23 = female pin header, 3 pins [form="♀ (female)"]

nets:
  N1: J15.pin1, J20.pin12, Thr-Sig.pad
  N2: J15.pin2, J20.pin11
  N3: J15.pin3, J20.pin10
  N4: J15.pin4, J20.pin9
  N5: J15.pin5, J20.pin8
  N6: J15.pin6, J20.pin7
  N7: J16.pin4, J20.pin15, Qwiic.2, DS3231M_2.3v3, 0_1uF.0, Thr-Pos.pad, LV.pin4
  N8: J16.pin6, J16.pin7, J18.pin4, J20.pin13, J21.pin4, Qwiic.1, DS3231M_2.GND, 1uF_2.0, 0_1uF.1, BAT3.-, ESC.1, J22.pin1, Thr-Gnd.pad, HV3.pin1, LV.pin1, J23.pin3
  N9: J16.pin8, J19.pin10, Pad2.pad
  N10: J17.pin2, J19.pin4
  N11: J17.pin3, J19.pin3
  N12: J17.pin4, J20.pin1
  N13: J17.pin5, LV.pin2
  N14: J17.pin6, LV.pin3
  N15: J17.pin7, J20.pin2, ESC.3
  N16: J17.pin8, J20.pin3, ESC.4
  N17: J18.pin1, Qwiic.4
  N18: J18.pin2, Qwiic.3
  N19: J18.pin5, J19.pin9
  N20: J18.pin6, J19.pin8
  N21: J18.pin7, J19.pin7
  N22: J18.pin8, J19.pin6
  N23: J18.pin9, J19.pin5
  N24: J19.pin1, DS3231M_2.SDA, 4k7_4.1
  N25: J19.pin2, DS3231M_2.SCL, 4k7_3.1
  N26: J19.pin12, J21.pin6
  N27: J20.pin4, J21.pin1
  N28: J20.pin5, J21.pin5
  N29: J20.pin6, J21.pin2
  N30: J20.pin16, J21.pin3
  N31: DS3231M.2, 1uF.1, 4k7.1, 4k7_2.1
  N32: DS3231M.7, 4k7_2.0
  N33: DS3231M.8, 4k7.0
  N34: DS3231M_2.VBatt, 1uF_2.1, BAT3.+#5, BAT3.+#6
  N35: 4k7_3.0, 4k7_4.0
  N36: BAT3.+#0, BAT3.+#4
  N37: ESC.2, Pad1.pad
  N38: J22.pin2, HV3.pin3
  N39: J22.pin3, HV3.pin4, J23.pin1
  N40: HV3.pin2, J23.pin2

notes:
  D4
  Rst
  GND
  A0
  AREF
  3v3
  A2
  A4
  MOSI
  MISO
  SCK
  A3
  A1
  A5
  Tx
  Rx
  En
  Batt
  D11
  D9
  SCL
  SDA
  D5
  D10
  D12
  D8
  D13
  Vusb
  D6
  5v
  IOREF
  N/C
  RST
  Vin
  D7
  D3
  D2

custom parts:
  Adafruit Metro M4 AirLift Lite: This is the Adafruit Metro M4 AirLift and Metro AirLift Lite, a Metro M4 with an ESP32 WiFi co-processor built in!
  Qwiic JST: Header 4 Standard 4-pin 0.1 header. Use with straight break away headers (SKU : PRT-00116), right angle break away headers (PRT-00553), swiss pins (PRT-00743), machine pins (PRT-00117), and female headers (PRT-00115). Molex polarized connector foot print use with SKU : PRT-08231 with associated crimp pins and housings. 1MM SMD Version SKU: PRT-10208
  Battery Holders: Battery Holders Various common sizes : AA, AAA, 20mm coin cell and 12mm coin cell.
