# Fritzing sketch Scoots_M4AirliftLite_2_3.5TFT_Feather_Shield_v2 (saved by Fritzing 0.9.3b)
circuit board: 7.15318cm x 5.2cm
breadboards: 1

parts:
  Part1 = Adafruit Metro M4 AirLift Lite [part_number="Adafruit #4000"]  # not connected
  J15 = female pin header, 6 pins [form="♀ (female)"]
  J16 = female pin header, 8 pins [form="♀ (female)"]
  J17 = female pin header, 8 pins [form="♀ (female)"]
  J18 = female pin header, 10 pins [form="♀ (female)"]
  J21 = double row female pin header, 6 pins [form="♀ (female)"]
  Qwiic = Qwiic JST [package=1x04-1mm-ra]
  Qwiic_2 = Qwiic JST [package=1x04-1mm-ra]  # not connected
  LV1 = female pin header, 6 pins [form="♀ (female)"]  # not connected
  HV1 = female pin header, 6 pins [form="♀ (female)"]  # not connected
  DS3231M = SO08 [chip_label=DS3231M package=SO]
  1uF = Ceramic Capacitor [capacitance=1µF package="1206 [SMD, multilayer]"]
  4k7 = Ceramic Capacitor [capacitance=1µF package="1206 [SMD, multilayer]"]
  4k7_2 = Ceramic Capacitor [capacitance=1µF package="1206 [SMD, multilayer]"]
  DS3231M_2 = SO08 [chip_label=DS3231M package=SO]
  4k7_3 = Ceramic Capacitor [capacitance=1µF package="1206 [SMD, multilayer]"]
  4k7_4 = Ceramic Capacitor [capacitance=1µF package="1206 [SMD, multilayer]"]
  1uF_2 = Ceramic Capacitor [capacitance=1µF package="1206 [SMD, multilayer]"]
  0_1uF = Ceramic Capacitor [capacitance=0.1µF package="1206 [SMD, multilayer]"]
  BAT3 = Battery Holders [package=battcon_20mm_4legs]
  ESC = Qwiic JST [package=1x04-1mm-ra]
  Thr-Sig = Pad [width=2.7657777777777888 height=1.6368888888888919 connect=center]
  Thr-Pos = Pad [width=2.7657777777777888 height=1.6368888888888919 connect=center]
  Thr-Gnd = Pad [width=2.7657777777777888 height=1.6368888888888919 connect=center]
  Pad2 = Pad [width=0.84666666666665868 height=0.90311111111111386 connect=center]
  Pad1 = Pad [width=0.84666666666665868 height=0.90311111111111386 connect=center]
  J24 = female pin header, 3 pins [form="♀ (female)"]  # not connected
  J25 = female pin header, 3 pins [form="♀ (female)"]  # not connected
  LV2 = female pin header, 4 pins [form="♀ (female)"]  # not connected
  HV4 = female pin header, 4 pins [form="♀ (female)"]  # not connected
  J26 = female pin header, 12 pins [form="♀ (female)"]
  J28 = female pin header, 16 pins [form="♀ (female)"]
  Part2 = RFM69W

nets:
  N1: J15.pin1, Thr-Sig.pad, J28.pin12
  N2: J15.pin2, J28.pin11
  N3: J15.pin3, J28.pin10
  N4: J15.pin4, J28.pin9
  N5: J15.pin5, J28.pin8
  N6: J15.pin6, J28.pin7
  3V3: J16.pin4, Qwiic.2, DS3231M_2.3v3, 0_1uF.0, Thr-Pos.pad, J28.pin15, Part2.3V3
  GND: J16.pin6, J16.pin7, J18.pin4, J21.pin4, Qwiic.1, DS3231M_2.GND, 1uF_2.0, 0_1uF.1, BAT3.-, ESC.1, Thr-Gnd.pad, J28.pin13, Part2.GND
  N7: J16.pin8, Pad2.pad, J26.pin10
  N8: J17.pin2, J26.pin4
  N9: J17.pin3, J26.pin3
  N10: J17.pin4, J28.pin1
  N11: J17.pin7, ESC.3, J28.pin2
  N12: J17.pin8, ESC.4, J28.pin3
  N13: J18.pin1, Qwiic.4
  N14: J18.pin2, Qwiic.3
  N15: J18.pin5, J26.pin9
  N16: J18.pin6, J26.pin8
  N17: J18.pin7, J26.pin7
  N18: J18.pin8, J26.pin6
  N19: J18.pin9, J26.pin5
  N20: J21.pin1, J28.pin4, Part2.MISO
  N21: J21.pin2, J28.pin6, Part2.SCK
  N22: J21.pin5, J28.pin5, Part2.MOSI
  N23: J21.pin6, J26.pin12
  N24: DS3231M.2, 1uF.1, 4k7.1, 4k7_2.1
  N25: DS3231M.7, 4k7_2.0
  N26: DS3231M.8, 4k7.0
  N27: DS3231M_2.VBatt, 1uF_2.1, BAT3.+#5, BAT3.+#6
  N28: DS3231M_2.SDA, 4k7_4.1, J26.pin1
  N29: DS3231M_2.SCL, 4k7_3.1, J26.pin2
  N30: 4k7_3.0, 4k7_4.0
  N31: BAT3.+#0, BAT3.+#4
  N32: ESC.2, Pad1.pad

notes:
  D4
  Rst
  GND
  A0
  AREF
  3v3
  A2
  A4
  MOSI
  MISO
  SCK
  A3
  A1
  A5
  Tx
  Rx
  En
  Batt
  D11
  D9
  SCL
  SDA
  D5
  D10
  D12
  D8
  D13
  Vusb
  D6
  5v
  IOREF
  N/C
  RST
  Vin
  D7
  D3
  D2

custom parts:
  Adafruit Metro M4 AirLift Lite: This is the Adafruit Metro M4 AirLift and Metro AirLift Lite, a Metro M4 with an ESP32 WiFi co-processor built in!
  Qwiic JST: Header 4 Standard 4-pin 0.1 header. Use with straight break away headers (SKU : PRT-00116), right angle break away headers (PRT-00553), swiss pins (PRT-00743), machine pins (PRT-00117), and female headers (PRT-00115). Molex polarized connector foot print use with SKU : PRT-08231 with associated crimp pins and housings. 1MM SMD Version SKU: PRT-10208
  Battery Holders: Battery Holders Various common sizes : AA, AAA, 20mm coin cell and 12mm coin cell.
