# Fritzing sketch Scoots_M4AirliftLite_2_Feather_Shield (saved by Fritzing 0.9.3b)
circuit board: 6cm x 5.2cm
breadboards: 1

parts:
  Part1 = Adafruit Metro M4 AirLift Lite [part_number="Adafruit #4000"]  # not connected
  J15 = female pin header, 6 pins [form="♀ (female)"]
  J16 = female pin header, 8 pins [form="♀ (female)"]
  J17 = female pin header, 8 pins [form="♀ (female)"]
  J18 = female pin header, 10 pins [form="♀ (female)"]
  J19 = female pin header, 12 pins [form="♀ (female)"]
  J20 = female pin header, 16 pins [form="♀ (female)"]
  J21 = double row female pin header, 6 pins [form="♀ (female)"]
  ESC = Qwiic JST [package=1x04-1mm-ra]  # not connected
  Qwiic = Qwiic JST [package=1x04-1mm-ra]  # not connected
  Qwiic_2 = Qwiic JST [package=1x04-1mm-ra]  # not connected
  Batt_- = Pad [width=2.25 height=2.25 connect=center]  # not connected
  CR12x2_Battery = Pad [width=2.25 height=2.25 connect=center]  # not connected
  Batt_+ = Pad [width=2.25 height=2.25 connect=center]  # not connected
  LV1 = female pin header, 6 pins [form="♀ (female)"]  # not connected
  HV1 = female pin header, 6 pins [form="♀ (female)"]  # not connected
  DS3231M = SO08 [chip_label=DS3231M package=SO]
  1uF = Ceramic Capacitor [capacitance=1µF package="1206 [SMD, multilayer]"]
  4k7 = Ceramic Capacitor [capacitance=1µF package="1206 [SMD, multilayer]"]
  4k7_2 = Ceramic Capacitor [capacitance=1µF package="1206 [SMD, multilayer]"]

nets:
  N1: J15.pin1, J20.pin12
  N2: J15.pin2, J20.pin11
  N3: J15.pin3, J20.pin10
  N4: J15.pin4, J20.pin9
  N5: J15.pin5, J20.pin8
  N6: J15.pin6, J20.pin7
  N7: J16.pin4, J20.pin15, DS3231M.2, 1uF.1, 4k7.1, 4k7_2.1
  N8: J16.pin6, 1uF.0
  N9: J17.pin3, J19.pin3
  N10: J17.pin4, J20.pin1
  N11: J17.pin7, J20.pin2
  N12: J17.pin8, J20.pin3
  N13: J18.pin1, J19.pin2, DS3231M.8, 4k7.0
  N14: J18.pin2, J19.pin1, DS3231M.7, 4k7_2.0
  N15: J18.pin5, J19.pin9
  N16: J18.pin6, J19.pin8
  N17: J18.pin7, J19.pin7
  N18: J18.pin8, J19.pin6
  N19: J18.pin9, J19.pin5
  N20: J18.pin10, J19.pin4
  N21: J19.pin12, J21.pin6
  N22: J20.pin4, J21.pin1
  N23: J20.pin5, J21.pin5
  N24: J20.pin6, J21.pin2
  N25: J20.pin13, J21.pin4
  N26: J20.pin16, J21.pin3

notes:
  D4
  Rst
  GND
  A0
  AREF
  3v3
  A2
  A4
  MOSI
  MISO
  SCK
  A3
  A1
  A5
  Tx
  Rx
  En
  Batt
  D11
  D9
  SCL
  SDA
  D5
  D10
  D12
  D8
  D13
  Vusb
  5v
  IOREF
  N/C
  RST
  Vin
  D7
  D6
  D3
  D2

custom parts:
  Adafruit Metro M4 AirLift Lite: This is the Adafruit Metro M4 AirLift and Metro AirLift Lite, a Metro M4 with an ESP32 WiFi co-processor built in!
  Qwiic JST: Header 4 Standard 4-pin 0.1 header. Use with straight break away headers (SKU : PRT-00116), right angle break away headers (PRT-00553), swiss pins (PRT-00743), machine pins (PRT-00117), and female headers (PRT-00115). Molex polarized connector foot print use with SKU : PRT-08231 with associated crimp pins and housings. 1MM SMD Version SKU: PRT-10208
