# Fritzing sketch Wii_Joystick_replacement_v3 (saved by Fritzing 0.9.3b)
circuit board: 2.33cm x 5.6cm
breadboards: 1

parts:
  Joystick = Thumb Joystick [package=joystick]
  GZC = Qwiic JST [package=1x04-1mm-ra]
  Qwiic = Qwiic JST [package=1x04-1mm-ra]
  J6 = female pin header, 12 pins [form="♀ (female)"]
  J7 = female pin header, 15 pins [form="♀ (female)"]
  Part2 = Adafruit Feather M0 RFM69 [part_number="Adafruit #3176 or #3177"]  # not connected
  PWR = Header 2 [package=jst-2-smd]
  Pwr_Sw = female pin header, 2 pins [form="♀ (female)"]
  Pad1 = Pad [width=0.28222222222222221 height=1.8 connect=center]
  J8 = female pin header, 9 pins [form="♀ (female)"]  # not connected

nets:
  N1: Joystick.SEL+, J6.pin3
  N2: Joystick.V+, Joystick.H+, Qwiic.2, J7.pin15
  N3: Joystick.SEL-, Joystick.H-, Joystick.V-, GZC.1, GZC.4, Qwiic.1, J7.pin13, PWR.2
  N4: Joystick.V, J7.pin12
  N5: Joystick.H, J7.pin11
  N6: GZC.2, J6.pin5
  N7: GZC.3, J6.pin4
  N8: Qwiic.3, J6.pin1
  N9: Qwiic.4, J6.pin2
  N10: J6.pin12, PWR.1, Pwr_Sw.pin1, Pwr_Sw.pin2, Pad1.pad

notes:
  eMB Controller v3
  NyKo Kama Wiichuk
  HighJinx's
  Adafruit M0 RFM69HCW
  RadioFeather
  D6 - Zbtn
  D7 - Cbtn
  D5 - Jbtn
  A0 - Vert
  A1 - Horz

custom parts:
  Qwiic JST: Header 4 Standard 4-pin 0.1 header. Use with straight break away headers (SKU : PRT-00116), right angle break away headers (PRT-00553), swiss pins (PRT-00743), machine pins (PRT-00117), and female headers (PRT-00115). Molex polarized connector foot print use with SKU : PRT-08231 with associated crimp pins and housings. 1MM SMD Version SKU: PRT-10208
  Adafruit Feather M0 RFM69: This is the Adafruit Feather M0 RFM69 Packet Radio - our take on an microcontroller with a RFM69HCW packet radio transceiver plus built in USB and battery charging. Its an Adafruit Feather M0 with a 433MHz or 900MHz radio module cooked in! We have other boards in the Feather family, check'em out here. At the Feather M0's heart is an ATSAMD21G18 ARM Cortex M0 processor, clocked at 48 MHz and at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
